# Fritzing sketch L293D PCB (saved by Fritzing 0.8.0b)
breadboards: 1

parts:
  l293 = H-Bridge [package=THT]
  NPN1 = NPN-Transistor [package="TO92 [THT]"]
  1k = Resistor [tolerance=±5% resistance=1k package=THT]
  1k_2 = Resistor [tolerance=±5% resistance=1k package=THT]
  10k2 = Resistor [tolerance=±5% resistance=10k package=THT]
  +5v = rounded female pin header, 1 pin [form="♀ (female rounded)"]
  control_1 = rounded female pin header, 1 pin [form="♀ (female rounded)"]
  gnd = rounded female pin header, 1 pin [form="♀ (female rounded)"]
  gnd1 = rounded female pin header, 1 pin [form="♀ (female rounded)"]
  control_2 = rounded female pin header, 1 pin [form="♀ (female rounded)"]
  R3Motor = rounded female pin header, 1 pin [form="♀ (female rounded)"]
  L3Motor = rounded female pin header, 1 pin [form="♀ (female rounded)"]
  L6Motor = rounded female pin header, 1 pin [form="♀ (female rounded)"]
  +5-30V = rounded female pin header, 1 pin [form="♀ (female rounded)"]
  +5v1 = rounded female pin header, 1 pin [form="♀ (female rounded)"]
  10k = Resistor [tolerance=±5% resistance=10k package=THT]
  NPN2 = NPN-Transistor [package="TO92 [THT]"]
  R6Motor = rounded female pin header, 1 pin [form="♀ (female rounded)"]

nets:
  N1: l293.1_2EN, l293.VCC1, +5v.pin1
  N2: l293.1A, 1k_2.Pin_0, control_1.pin1
  N3: l293.1Y, L3Motor.pin1
  GND1: l293.GND1, l293.GND2, NPN1.E, gnd.pin1
  N4: l293.2Y, L6Motor.pin1
  N5: l293.2A, NPN1.C, 10k.Pin_0
  N6: l293.VCC2, +5-30V.pin1
  N7: l293.3_4EN, 10k2.Pin_0, +5v1.pin1, 10k.Pin_1
  N8: l293.3A, 10k2.Pin_1, NPN2.E
  N9: l293.3Y, R6Motor.pin1
  GND3: l293.GND3, l293.GND4, gnd1.pin1, NPN2.C
  N10: l293.4Y, R3Motor.pin1
  N11: l293.4A, 1k.Pin_1, control_2.pin1
  N12: NPN1.B, 1k_2.Pin_1
  N13: 1k.Pin_0, NPN2.B
